// Logisim project op_select_SOP_KMAP.circ as structural Verilog: 1 circuit, main circuit main
module main (
  input  OP0,
  input  OP1,
  input  OP2,
  output valid_OP
);

  xor xor_1 (valid_OP, OP2, OP1);
endmodule
